// Logisim project 16x4_mux.circ as structural Verilog: 1 circuit, main circuit main
module main (
  input  S1,
  input  S0,
  input  A3,
  input  A2,
  input  A1,
  input  A0,
  input  B3,
  input  B2,
  input  B1,
  input  B0,
  input  C3,
  input  C2,
  input  C1,
  input  C0,
  input  D3,
  input  D2,
  input  D1,
  input  D0,
  output Out3,
  output Out2,
  output Out1,
  output Out0
);

  wire and_1_out, and_2_out, and_3_out, and_4_out, and_5_out, and_6_out, and_7_out, and_8_out, and_9_out,
       and_10_out, and_11_out, and_12_out, and_13_out, and_14_out, and_15_out, and_16_out;

  and and_1 (and_1_out, ~S1, ~S0, A3);  // AND_Gate
  and and_2 (and_2_out, ~S1, S0, B3);  // AND_Gate
  and and_3 (and_3_out, S1, ~S0, C3);  // AND_Gate
  and and_4 (and_4_out, S1, S0, D3);
  and and_5 (and_5_out, ~S1, ~S0, A2);  // AND_Gate
  and and_6 (and_6_out, ~S1, S0, B2);  // AND_Gate
  and and_7 (and_7_out, S1, ~S0, C2);  // AND_Gate
  and and_8 (and_8_out, S1, S0, D2);
  and and_9 (and_9_out, ~S1, ~S0, A1);  // AND_Gate
  and and_10 (and_10_out, ~S1, S0, B1);  // AND_Gate
  and and_11 (and_11_out, S1, ~S0, C1);  // AND_Gate
  and and_12 (and_12_out, S1, S0, D1);
  and and_13 (and_13_out, ~S1, ~S0, A0);  // AND_Gate
  and and_14 (and_14_out, ~S1, S0, B0);  // AND_Gate
  and and_15 (and_15_out, S1, ~S0, C0);  // AND_Gate
  and and_16 (and_16_out, S1, S0, D0);
  or or_1 (Out3, and_1_out, and_2_out, and_3_out, and_4_out);
  or or_2 (Out2, and_5_out, and_6_out, and_7_out, and_8_out);
  or or_3 (Out1, and_9_out, and_10_out, and_11_out, and_12_out);
  or or_4 (Out0, and_13_out, and_14_out, and_15_out, and_16_out);
endmodule
